# Fritzing sketch shield_garoa_status (saved by Fritzing 0.7.1b)
breadboards: 1

parts:
  Arduino1 = Arduino
  C1 = Tantalum Capacitor [capacitance=47nF package="200 mil [THT, tantalum]"]
  J1 = screw terminal, 2 pins

nets:
  N1: Arduino1.GND, C1.-, J1.pin1
  N2: Arduino1.D3, J1.pin2
  N3: Arduino1.RST, C1.+

notes:
  Garoa Status API
  abril/2012
